# Fritzing sketch projectDiagram (saved by Fritzing 0.9.3b)

parts:
  Part1 = Arduino Pro Micro (Clone)
  Part2 = Bluetooth HC-05 Macho
  X2 = USB Connectors [package=usb-a-pcb]

nets:
  N1: Part1.TXO, Part2.RXD
  N2: Part1.RXI, Part2.TXD
  GND: Part1.GND, Part2.GND
  N3: Part1.D3, X2.D-
  N4: Part1.D4, X2.D+
  N5: Part1.D9, Part1.RST
  VCC: Part1.VCC, Part2.VCC
